// Logisim project PX16C.circ as structural Verilog: 3 circuits, main circuit main
module main (
);

  wire A_out, AADD, Act, adder_1_cout, Addr, AIA, AIB, and_1_p2, and_2_out, and_3_p1, and_3_p2, and_3_p4,
       and_4_p1, and_4_p2, and_5_out, and_6_out, and_7_p2, and_8_p5, and_9_p5, and_9_p6, and_10_p6,
       and_11_p5, and_12_out, and_13_p3, and_14_out, and_16_out, and_19_out, and_20_out, and_25_out,
       and_26_p2, and_26_p6, and_27_p5, and_28_p3, and_29_out, and_30_p2, and_33_out, and_34_p3, AOR, ASHL,
       ASHR, AXA, AXB, AXOR, B_out, Boot_0, Boot_1, button_1_out, button_2_out, button_4_out, button_5_out,
       button_6_out, Cin, CLK, CMP, comparator_1_lt, comparator_3_eq, comparator_3_gt, comparator_3_lt,
       comparator_5_eq, comparator_5_gt, comparator_5_lt, comparator_6_gt, comparator_6_lt, comparator_7_eq,
       comparator_7_gt, comparator_7_lt, comparator_8_eq, comparator_9_eq, comparator_10_eq,
       comparator_11_eq, comparator_12_eq, comparator_13_eq, Cond_met, Cout, CX, decoder_1_out0,
       decoder_1_out1, decoder_1_out2, decoder_1_out3, decoder_1_out4, decoder_1_out6, decoder_1_out7,
       decoder_2_out0, decoder_2_out1, decoder_2_out2, decoder_2_out3, decoder_2_out4, decoder_2_out5,
       decoder_2_out6, decoder_2_out7, decoder_3_out0, decoder_3_out1, decoder_3_out2, decoder_3_out3,
       decoder_3_out4, decoder_3_out5, decoder_3_out6, decoder_4_out0, decoder_4_out1, decoder_4_out4,
       demultiplexer_1_out0, demultiplexer_1_out1, demultiplexer_2_out0, demultiplexer_2_out1,
       demultiplexer_3_out0, demultiplexer_4_out0, demultiplexer_4_out1, demultiplexer_5_out0,
       demultiplexer_5_out1, demultiplexer_6_out1, demultiplexer_7_out1, demultiplexer_9_out1,
       demultiplexer_10_out0, demultiplexer_10_out1, demultiplexer_12_out0, demultiplexer_12_out1, Flag_Cout,
       Flag_SCout, Flag_Zero, INC, INT_prog, Intr, IRQ, IRQ_Enable, Is_CX, Is_INTR, Is_JSR, Is_LEA, Is_ST,
       IY, Jsr, Load_0, Load_1, Load_2, Mov, multiplexer_6_out, multiplexer_11_out, multiplexer_12_out,
       multiplexer_13_out, nand_1_p2, nand_1_p4, nand_2_out, nand_3_out, nand_4_out, NMI, NMI_Enable,
       No_Button_Wake, No_Timer_Wake, nor_2_p2, nor_3_out, not_2_out, not_3_out, not_4_out, not_5_out,
       not_6_out, not_8_out, not_9_out, not_10_out, not_11_out, or_3_out, or_5_out, or_6_out, or_7_out,
       or_8_out, or_10_out, or_11_p2, or_12_p2, or_13_out, or_16_out, or_17_p3, or_18_out, or_20_out,
       or_22_p3, or_23_p3, or_24_out, or_25_out, or_26_out, or_28_out, or_29_p2, or_30_out, or_37_out, Pop,
       Push, R4, R6, RM, Rp, RST, s_r_ff_1_q, SAr, SCout, Screen_Disable, Sel_out, Si0, Si1, Sleep_Deep,
       Sleep_Idle, Sleep_Light, Sta_out, TCLK, Timer_Ack, Timer_Enable, Timer_IRQ, Timer_NMI, Timer_Read,
       Timer_Write, undriven, v_out, WM, WPF, WR, X_out, xor_7_p4, xor_8_out, Y_out, Zero;
  wire [0:0] PS_q;
  wire [2:0] A, B, D, IA, IB, IX, multiplexer_3_out, multiplexer_4_out, multiplexer_9_out, multiplexer_10_out;
  wire [2:2] or_21_out;
  wire [5:0] IOp;
  wire [6:0] keyboard_1_data;
  wire [7:3] controlled_buffer_38_out, Mode_q;
  wire [11:2] or_19_out;
  wire [12:2] PF, pull_resistor_3_node;
  wire [14:14] xor_1_out_2;
  wire [15:0] Ab, adder_1_out, AR_q, bit_extender_1_out, bit_extender_2_out, bit_extender_3_out,
       bit_extender_4_out, button_inputs_1_data_out, controlled_buffer_19_out, controlled_buffer_21_out,
       controlled_buffer_22_out, Db, imm0_q, imm1_q, Limit_High_q, Limit_Low_q, multiplexer_2_out,
       multiplexer_7_out, multiplexer_8_out, n32x16_screen_controller_1_col_0,
       n32x16_screen_controller_1_col_1, n32x16_screen_controller_1_col_2, n32x16_screen_controller_1_col_3,
       n32x16_screen_controller_1_col_4, n32x16_screen_controller_1_col_5, n32x16_screen_controller_1_col_6,
       n32x16_screen_controller_1_col_7, n32x16_screen_controller_1_col_8, n32x16_screen_controller_1_col_9,
       n32x16_screen_controller_1_col_10, n32x16_screen_controller_1_col_11,
       n32x16_screen_controller_1_col_12, n32x16_screen_controller_1_col_13,
       n32x16_screen_controller_1_col_14, n32x16_screen_controller_1_col_15,
       n32x16_screen_controller_1_col_16, n32x16_screen_controller_1_col_17,
       n32x16_screen_controller_1_col_18, n32x16_screen_controller_1_col_19,
       n32x16_screen_controller_1_col_20, n32x16_screen_controller_1_col_21,
       n32x16_screen_controller_1_col_22, n32x16_screen_controller_1_col_23,
       n32x16_screen_controller_1_col_24, n32x16_screen_controller_1_col_25,
       n32x16_screen_controller_1_col_26, n32x16_screen_controller_1_col_27,
       n32x16_screen_controller_1_col_28, n32x16_screen_controller_1_col_29,
       n32x16_screen_controller_1_col_30, n32x16_screen_controller_1_col_31, not_1_out, or_2_p3, or_4_out,
       PbA, PbB, PC_q, pull_resistor_4_node, R0_q, R1_q, R2_q, R3_q, Rb, rom_1_data, ST_q, Temp_High_q,
       Temp_Low_q, Timer_q, Timer_q_2, xor_2_out, xor_3_out, xor_4_out, xor_5_out, xor_6_out;
  wire [15:1] xor_1_out;

  // Probe on PbA
  DotMatrix #(.inputtype("row"), .matrixcols(8), .matrixrows(2), .dotshape("circle")) dotmatrix_1 (
    .row0(PbA[15:8]), .row1(PbA[7:0]));
  // Probe on PbB
  DotMatrix #(.inputtype("row"), .matrixcols(8), .matrixrows(2), .dotshape("circle")) dotmatrix_2 (
    .row0(PbB[15:8]), .row1(PbB[7:0]));
  // Probe on Rb
  DotMatrix #(.inputtype("row"), .matrixcols(8), .matrixrows(2), .dotshape("circle")) dotmatrix_3 (
    .row0(Rb[15:8]), .row1(Rb[7:0]));
  // Probe on Db
  DotMatrix #(.inputtype("row"), .matrixcols(8), .matrixrows(2), .dotshape("circle")) dotmatrix_4 (
    .row0(Db[15:8]), .row1(Db[7:0]));
  // Probe on Ab
  DotMatrix #(.inputtype("row"), .matrixcols(8), .matrixrows(2), .dotshape("circle")) dotmatrix_5 (
    .row0(Ab[15:8]), .row1(Ab[7:0]));
  Button button_1 (.out(button_1_out));
  Button button_2 (.out(button_2_out));
  // Probe on PbA
  // Probe on PbB
  // Probe on Rb
  // Probe on Db
  // Probe on Ab
  or or_1 (WM, decoder_1_out7, decoder_1_out7);
  buf buffer_1 (IRQ, button_1_out);
  buf buffer_2 (NMI, button_2_out);
  Button button_3 (.out(RST));
  // AND_Gate and_1: pin names not known; wires that end beside it: RST, and_1_p2, CLK
  Clock clock_1 (.out(and_1_p2));
  Decoder #(.select(3), .disabled(0), .enable("true")) decoder_1 (
    .out0(decoder_1_out0), .out1(decoder_1_out1), .out2(decoder_1_out2), .out3(decoder_1_out3),
    .out4(decoder_1_out4), .out5(WPF), .out6(decoder_1_out6), .out7(decoder_1_out7), .sel(D), .en(WR));
  Register #(.width(16)) R0 (.D(Db), .en(decoder_1_out0), .Q(R0_q), .clk(CLK), .clr(RST));
  Register #(.width(16)) R1 (.D(Db), .en(decoder_1_out1), .Q(R1_q), .clk(CLK), .clr(RST));
  Register #(.width(16)) R2 (.D(Db), .en(decoder_1_out2), .Q(R2_q), .clk(CLK), .clr(RST));
  Register #(.width(16)) R3 (.D(Db), .en(decoder_1_out3), .Q(R3_q), .clk(CLK), .clr(RST));
  Register #(.width(16)) ST (.D(Db), .en(decoder_1_out4), .Q(ST_q), .clk(CLK), .clr(RST));
  Counter #(.width(16), .max('hffff)) PC (
    .load(decoder_1_out6), .D(Db), .count(INC), .Q(PC_q), .clk(CLK), .clr(RST));  // open: carry
  Register #(.width(16)) imm0 (.D(Db), .en(Si0), .Q(imm0_q), .clk(CLK), .clr(RST));
  Register #(.width(16)) imm1 (.D(Db), .en(Si1), .Q(imm1_q), .clk(CLK), .clr(RST));
  and and_2 (and_2_out, CLK, WM);
  Comparator #(.width(16), .mode("unsigned")) comparator_1 (
    .a(Ab), .b(16'h8000), .lt(comparator_1_lt));  // open: gt, eq
  // AND_Gate and_3: pin names not known; wires that end beside it: and_3_p1, and_3_p2, comparator_1_lt, and_3_p4, RM
  Comparator #(.width(16), .mode("unsigned")) comparator_2 (
    .a(Ab), .b(not_1_out), .gt(and_3_p2), .lt(and_3_p1));  // open: eq
  assign not_1_out = ~16'h40;  // NOT_Gate not_1, 16 bits wide
  assign PbA = decoder_2_out0 ? R0_q : 16'bz;  // Controlled_Buffer controlled_buffer_1
  assign PbB = decoder_3_out0 ? R0_q : 16'bz;  // Controlled_Buffer controlled_buffer_2
  assign PbA = decoder_2_out1 ? R1_q : 16'bz;  // Controlled_Buffer controlled_buffer_3
  assign PbB = decoder_3_out1 ? R1_q : 16'bz;  // Controlled_Buffer controlled_buffer_4
  assign PbA = decoder_2_out2 ? R2_q : 16'bz;  // Controlled_Buffer controlled_buffer_5
  assign PbB = decoder_3_out2 ? R2_q : 16'bz;  // Controlled_Buffer controlled_buffer_6
  assign PbA = decoder_2_out3 ? R3_q : 16'bz;  // Controlled_Buffer controlled_buffer_7
  assign PbB = decoder_3_out3 ? R3_q : 16'bz;  // Controlled_Buffer controlled_buffer_8
  assign PbA = decoder_2_out4 ? ST_q : 16'bz;  // Controlled_Buffer controlled_buffer_9
  assign PbB = decoder_3_out4 ? ST_q : 16'bz;  // Controlled_Buffer controlled_buffer_10
  assign PbA = decoder_2_out5 ? {Flag_SCout, Flag_Cout, Flag_Zero, PF[12:5], INT_prog, PF[3:2], IRQ_Enable, NMI_Enable} : 16'bz;  // Controlled_Buffer controlled_buffer_11
  assign PbB = decoder_3_out5 ? {Flag_SCout, Flag_Cout, Flag_Zero, PF[12:5], INT_prog, PF[3:2], IRQ_Enable, NMI_Enable} : 16'bz;  // Controlled_Buffer controlled_buffer_12
  assign PbA = decoder_2_out6 ? PC_q : 16'bz;  // Controlled_Buffer controlled_buffer_13
  assign PbB = decoder_3_out6 ? PC_q : 16'bz;  // Controlled_Buffer controlled_buffer_14
  assign PbA = decoder_2_out7 ? imm0_q : 16'bz;  // Controlled_Buffer controlled_buffer_15
  assign PbB = and_5_out ? imm0_q : 16'bz;  // Controlled_Buffer controlled_buffer_16
  assign PbB = and_4_p1 ? imm1_q : 16'bz;  // Controlled_Buffer controlled_buffer_17
  // AND_Gate and_4: pin names not known; wires that end beside it: and_4_p1, and_4_p2
  Decoder #(.select(3), .disabled(0)) decoder_2 (
    .out0(decoder_2_out0), .out1(decoder_2_out1), .out2(decoder_2_out2), .out3(decoder_2_out3),
    .out4(decoder_2_out4), .out5(decoder_2_out5), .out6(decoder_2_out6), .out7(decoder_2_out7), .sel(A),
    .en(and_5_out));
  and and_5 (and_5_out, IA[0], IA[1], IA[2], ~IY, Addr);  // AND_Gate
  ROM #(.addrWidth(16), .dataWidth(16)) rom_1 (.addr(Ab), .data(rom_1_data), .sel(1'b1));
  assign Db = and_6_out ? rom_1_data : 16'bz;  // Controlled_Buffer controlled_buffer_18
  assign controlled_buffer_19_out = WM ? Db : 16'bz;  // Controlled_Buffer controlled_buffer_19
  RAM #(.addrWidth(16), .dataWidth(16)) ram_1 (
    .addr(Ab), .data(controlled_buffer_19_out), .sel(1'b1), .clk(and_2_out), .ld(and_7_p2), .clr(RST));
  assign Db = and_7_p2 ? controlled_buffer_19_out : 16'bz;  // Controlled_Buffer controlled_buffer_20
  and and_6 (and_6_out, and_3_p4, comparator_1_lt, and_3_p4);
  // AND_Gate and_7: pin names not known; wires that end beside it: comparator_1_lt, and_7_p2
  Decoder #(.select(3), .disabled(0)) decoder_3 (
    .out0(decoder_3_out0), .out1(decoder_3_out1), .out2(decoder_3_out2), .out3(decoder_3_out3),
    .out4(decoder_3_out4), .out5(decoder_3_out5), .out6(decoder_3_out6), .out7(and_4_p2), .sel(B));  // open: en
  Pull_Resistor pull_resistor_1 (.node(Rb));
  DotMatrix #(.matrixcols(32), .matrixrows(16)) dotmatrix_6 (
    .col0(n32x16_screen_controller_1_col_0), .col1(n32x16_screen_controller_1_col_1),
    .col2(n32x16_screen_controller_1_col_2), .col3(n32x16_screen_controller_1_col_3),
    .col4(n32x16_screen_controller_1_col_4), .col5(n32x16_screen_controller_1_col_5),
    .col6(n32x16_screen_controller_1_col_6), .col7(n32x16_screen_controller_1_col_7),
    .col8(n32x16_screen_controller_1_col_8), .col9(n32x16_screen_controller_1_col_9),
    .col10(n32x16_screen_controller_1_col_10), .col11(n32x16_screen_controller_1_col_11),
    .col12(n32x16_screen_controller_1_col_12), .col13(n32x16_screen_controller_1_col_13),
    .col14(n32x16_screen_controller_1_col_14), .col15(n32x16_screen_controller_1_col_15),
    .col16(n32x16_screen_controller_1_col_16), .col17(n32x16_screen_controller_1_col_17),
    .col18(n32x16_screen_controller_1_col_18), .col19(n32x16_screen_controller_1_col_19),
    .col20(n32x16_screen_controller_1_col_20), .col21(n32x16_screen_controller_1_col_21),
    .col22(n32x16_screen_controller_1_col_22), .col23(n32x16_screen_controller_1_col_23),
    .col24(n32x16_screen_controller_1_col_24), .col25(n32x16_screen_controller_1_col_25),
    .col26(n32x16_screen_controller_1_col_26), .col27(n32x16_screen_controller_1_col_27),
    .col28(n32x16_screen_controller_1_col_28), .col29(n32x16_screen_controller_1_col_29),
    .col30(n32x16_screen_controller_1_col_30), .col31(n32x16_screen_controller_1_col_31));
  _32x16_screen_controller u_32x16_screen_controller_1 (
    .CLOCK(CLK), .RESET(RST), .Enable(WM), .Data(Db), .Adress(Ab), .Col_0(n32x16_screen_controller_1_col_0),
    .Col_1(n32x16_screen_controller_1_col_1), .Col_2(n32x16_screen_controller_1_col_2),
    .Col_3(n32x16_screen_controller_1_col_3), .Col_4(n32x16_screen_controller_1_col_4),
    .Col_5(n32x16_screen_controller_1_col_5), .Col_6(n32x16_screen_controller_1_col_6),
    .Col_7(n32x16_screen_controller_1_col_7), .Col_8(n32x16_screen_controller_1_col_8),
    .Col_9(n32x16_screen_controller_1_col_9), .Col_10(n32x16_screen_controller_1_col_10),
    .Col_11(n32x16_screen_controller_1_col_11), .Col_12(n32x16_screen_controller_1_col_12),
    .Col_13(n32x16_screen_controller_1_col_13), .Col_14(n32x16_screen_controller_1_col_14),
    .Col_15(n32x16_screen_controller_1_col_15), .Col_16(n32x16_screen_controller_1_col_16),
    .Col_17(n32x16_screen_controller_1_col_17), .Col_18(n32x16_screen_controller_1_col_18),
    .Col_19(n32x16_screen_controller_1_col_19), .Col_20(n32x16_screen_controller_1_col_20),
    .Col_21(n32x16_screen_controller_1_col_21), .Col_22(n32x16_screen_controller_1_col_22),
    .Col_23(n32x16_screen_controller_1_col_23), .Col_24(n32x16_screen_controller_1_col_24),
    .Col_25(n32x16_screen_controller_1_col_25), .Col_26(n32x16_screen_controller_1_col_26),
    .Col_27(n32x16_screen_controller_1_col_27), .Col_28(n32x16_screen_controller_1_col_28),
    .Col_29(n32x16_screen_controller_1_col_29), .Col_30(n32x16_screen_controller_1_col_30),
    .Col_31(n32x16_screen_controller_1_col_31));
  Button button_4 (.out(button_4_out));
  Button_inputs button_inputs_1 (
    .Left(button_4_out), .Up(button_5_out), .Down(v_out), .Right(button_6_out), .Start(Sta_out),
    .Select(Sel_out), .X(X_out), .A(A_out), .Y(Y_out), .B(B_out), .Clock(CLK), .Reset(RST),
    .Data_out(button_inputs_1_data_out));  // open: Clear_interrupt, Interrupt
  Comparator #(.width(16), .mode("unsigned")) comparator_3 (
    .a(Ab), .b(16'hfffd), .gt(comparator_3_gt), .eq(comparator_3_eq), .lt(comparator_3_lt));
  assign controlled_buffer_21_out = not_2_out ? PbA : 16'bz;  // Controlled_Buffer controlled_buffer_21
  assign controlled_buffer_22_out = not_3_out ? PbB : 16'bz;  // Controlled_Buffer controlled_buffer_22
  not not_2 (not_2_out, AXA);
  not not_3 (not_3_out, AXB);
  Register #(.width(16)) AR (.D(Rb), .en(SAr), .Q(AR_q), .clk(CLK), .clr(RST));
  Button button_5 (.out(button_5_out));
  Button button_6 (.out(button_6_out));
  Button v (.out(v_out));
  Button Sta (.out(Sta_out));
  // AND_Gate and_8: pin names not known; wires that end beside it: comparator_3_gt, comparator_3_eq, comparator_3_lt, RM, and_8_p5
  assign Db = and_8_p5 ? button_inputs_1_data_out : 16'bz;  // Controlled_Buffer controlled_buffer_23
  assign controlled_buffer_21_out = AXA ? {16{1'b0}} : 16'bz;  // Controlled_Buffer controlled_buffer_24
  assign controlled_buffer_22_out = AXB ? {16{1'b0}} : 16'bz;  // Controlled_Buffer controlled_buffer_25
  assign bit_extender_1_out = {{15{AIB}}, AIB};  // Bit_Extender bit_extender_1
  assign bit_extender_2_out = {{15{AIA}}, AIA};  // Bit_Extender bit_extender_2
  assign bit_extender_3_out = {{15{AIA}}, AIA};  // Bit_Extender bit_extender_3
  Comparator #(.width(16), .mode("unsigned")) comparator_4 (.a({16{1'b0}}), .b(Rb), .eq(Zero));  // open: gt, lt
  Multiplexer #(.width(16)) multiplexer_1 (.in0(Rb), .in1(AR_q), .out(Ab), .sel(WM));  // open: en
  not not_4 (not_4_out, RM);
  assign Db = not_4_out ? Rb : 16'bz;  // Controlled_Buffer controlled_buffer_26
  Pull_Resistor pull_resistor_2 (.node(Db));
  Button X (.out(X_out));
  Button u_A (.out(A_out));
  Button Sel (.out(Sel_out));
  ExactlyOne xor_1[15:0] (
    .out({xor_1_out_2[14], xor_1_out}), .in1(controlled_buffer_21_out), .in3(bit_extender_2_out),
    .in4(controlled_buffer_22_out));
  ExactlyOne xor_2[15:0] (
    .out(xor_2_out), .in0(bit_extender_2_out), .in1(controlled_buffer_22_out), .in3(bit_extender_1_out));
  Pull_Resistor pull_resistor_3 (.node({SCout, Cout, Zero, pull_resistor_3_node[12:5], INT_prog, pull_resistor_3_node[3:2], IRQ_Enable, NMI_Enable}));
  Button Y (.out(Y_out));
  Button u_B (.out(B_out));
  Adder #(.width(16)) adder_1 (
    .a({xor_1_out_2[14], xor_1_out}), .b(xor_2_out), .out(adder_1_out), .cin(Cin), .cout(adder_1_cout));
  ExactlyOne xor_3[15:0] (.out(xor_3_out), .in1({xor_1_out_2[14], xor_1_out}), .in3(16'h8000), .in4(xor_2_out));
  Adder #(.width(16)) adder_2 (.a(xor_3_out), .b(xor_4_out), .cin(Cin), .cout(SCout));  // open: out
  ExactlyOne xor_4[15:0] (.out(xor_4_out), .in0(16'h8000), .in1(xor_2_out), .in3(16'h8000));
  assign xor_5_out = {xor_1_out_2[14], xor_1_out} ^ xor_2_out;  // XOR_Gate xor_5, 16 bits wide
  // OR_Gate #(.width(16)) or_2: pin names not known; wires that end beside it: {xor_1_out_2[14], xor_1_out}, xor_2_out, or_2_p3
  assign xor_6_out = or_2_p3 ^ bit_extender_3_out;  // XOR_Gate xor_6, 16 bits wide
  Pull_Resistor pull_resistor_4 (.node({pull_resistor_4_node[15:5], Intr, pull_resistor_4_node[3:0]}));
  Multiplexer #(.width(16)) multiplexer_2 (
    .in0({SCout, Cout, Zero, pull_resistor_3_node[12:5], INT_prog, pull_resistor_3_node[3:2], IRQ_Enable, NMI_Enable}),
    .in1(Db), .out(multiplexer_2_out), .sel(WPF));  // open: en
  or or_3 (or_3_out, WPF, Intr, Act);
  assign Rb = AADD ? adder_1_out : 16'bz;  // Controlled_Buffer controlled_buffer_27
  assign Cout = AADD ? adder_1_cout : 1'bz;  // Controlled_Buffer controlled_buffer_28
  Pull_Resistor pull_resistor_5 (.node(Cout));
  assign Rb = AXOR ? xor_5_out : 16'bz;  // Controlled_Buffer controlled_buffer_29
  assign Rb = AOR ? xor_6_out : 16'bz;  // Controlled_Buffer controlled_buffer_30
  assign Rb = ASHL ? {xor_1_out, Cin} : 16'bz;  // Controlled_Buffer controlled_buffer_31
  assign Cout = ASHL ? xor_1_out_2[14] : 1'bz;  // Controlled_Buffer controlled_buffer_32
  assign Rb = ASHR ? {Cin, xor_1_out_2[14], xor_1_out[15:2]} : 16'bz;  // Controlled_Buffer controlled_buffer_33
  assign Cout = ASHR ? xor_1_out[1] : 1'bz;  // Controlled_Buffer controlled_buffer_34
  assign bit_extender_4_out = {{15{xor_2_out[15]}}, xor_2_out[15]};  // Bit_Extender bit_extender_4
  assign Rb = CX ? bit_extender_4_out : 16'bz;  // Controlled_Buffer controlled_buffer_35
  assign or_4_out = {pull_resistor_4_node[15:5], Intr, pull_resistor_4_node[3:0]} | multiplexer_2_out;  // OR_Gate or_4, 16 bits wide
  Register #(.width(16)) u_PF (
    .D(or_4_out), .en(or_3_out),
    .Q({Flag_SCout, Flag_Cout, Flag_Zero, PF[12:5], INT_prog, PF[3:2], IRQ_Enable, NMI_Enable}), .clk(CLK),
    .clr(RST));
  Comparator #(.width(16), .mode("unsigned")) comparator_5 (
    .a(Ab), .b(16'hfff6), .gt(comparator_5_gt), .eq(comparator_5_eq), .lt(comparator_5_lt));
  // AND_Gate and_9: pin names not known; wires that end beside it: comparator_5_gt, comparator_5_eq, comparator_5_lt, WM, and_9_p5, and_9_p6
  Comparator #(.width(16), .mode("unsigned")) comparator_6 (
    .a(Ab), .b(16'hfff5), .gt(comparator_6_gt), .eq(and_9_p5), .lt(comparator_6_lt));
  // AND_Gate and_10: pin names not known; wires that end beside it: comparator_6_gt, and_9_p5, comparator_6_lt, WM, RM, and_10_p6
  Comparator #(.width(16), .mode("unsigned")) comparator_7 (
    .a(Ab), .b({16{1'b1}}), .gt(comparator_7_gt), .eq(comparator_7_eq), .lt(comparator_7_lt));
  // AND_Gate and_11: pin names not known; wires that end beside it: comparator_7_gt, comparator_7_eq, comparator_7_lt, RM, and_11_p5
  TTY #(.rows(11), .cols(40)) tty_1 (.data(Db[6:0]), .clk(CLK), .we(and_9_p6), .clr(RST));
  Keyboard #(.buflen(40)) keyboard_1 (.clk(CLK), .re(and_10_p6), .clr(RST), .data(keyboard_1_data));  // open: avail
  assign Db[6:0] = and_10_p6 ? keyboard_1_data : 7'bz;  // Controlled_Buffer controlled_buffer_36
  assign Db = and_11_p5 ? 16'h40 : 16'bz;  // Controlled_Buffer controlled_buffer_37
  and and_12 (and_12_out, Addr, nand_1_p4);
  // NAND_Gate nand_1: pin names not known; wires that end beside it: IX[0], nand_1_p2, IX[2], nand_1_p4
  or or_5 (or_5_out, Boot_0, Boot_1, Pop);
  or or_6 (or_6_out, Push, or_5_out);
  or or_7 (or_7_out, and_12_out, or_5_out, decoder_4_out0);
  Decoder #(.select(3), .disabled(0), .enable("true")) decoder_4 (
    .out0(decoder_4_out0), .out1(decoder_4_out1), .out2(CMP), .out3(AIA), .out4(decoder_4_out4), .out5(AXOR),
    .out6(ASHL), .out7(ASHR), .sel(IOp[2:0]), .en(Act));
  // AND_Gate and_13: pin names not known; wires that end beside it: IOp[4], Act, and_13_p3
  not not_5 (not_5_out, Load_0);
  Demultiplexer #(.disabled(0)) demultiplexer_1 (
    .out0(demultiplexer_1_out0), .out1(demultiplexer_1_out1), .in(Addr), .sel(IY));
  or or_8 (or_8_out, decoder_4_out1, Push, CMP);
  or or_9 (AXB, and_13_p3, or_6_out, or_6_out);
  or or_10 (or_10_out, or_6_out, or_6_out, Act);
  and and_14 (and_14_out, ~multiplexer_3_out[0], ~multiplexer_3_out[1], multiplexer_3_out[2]);  // AND_Gate
  Multiplexer #(.width(3)) multiplexer_3 (
    .in0(Db[11:9]), .in1(3'b111), .out(multiplexer_3_out), .sel(not_5_out));  // open: en
  // OR_Gate or_11: pin names not known; wires that end beside it: demultiplexer_1_out1, or_11_p2, Load_0
  Multiplexer #(.width(3)) multiplexer_4 (
    .in0(Db[8:6]), .in1(3'b111), .out(multiplexer_4_out), .sel(not_5_out));  // open: en
  // OR_Gate or_12: pin names not known; wires that end beside it: demultiplexer_1_out0, or_12_p2, Load_0
  nor nor_1 (AXA, Act, Push, or_7_out);
  not not_6 (not_6_out, or_7_out);
  // XOR_Gate xor_7: pin names not known; wires that end beside it: not_6_out, AXB, Flag_Cout, xor_7_p4
  Register #(.width(1)) Y_2 (.D(Db[15]), .en(Load_0), .Q(IY), .clk(CLK), .clr(RST));
  Register #(.width(3)) X_2 (.D(Db[14:12]), .en(Load_0), .Q(IX), .clk(CLK), .clr(RST));
  Register #(.width(3)) B_2 (.D(multiplexer_3_out), .en(or_11_p2), .Q(IB), .clk(CLK), .clr(RST));
  Register #(.width(3)) A_2 (.D(multiplexer_4_out), .en(or_12_p2), .Q(IA), .clk(CLK), .clr(RST));
  Register #(.width(6)) Opcode (.D(Db[5:0]), .en(Load_0), .Q(IOp), .clk(CLK), .clr(RST));
  Register #(.width(1)) Y_3 (.D(and_14_out), .en(Load_0), .Q(Is_ST), .clk(CLK), .clr(RST));
  or or_13 (or_13_out, AXA, or_7_out, or_8_out);
  // OR_Gate or_14: pin names not known; wires that end beside it: or_8_out, AIA, AIB
  // OR_Gate or_15: pin names not known; wires that end beside it: or_8_out, AIA, decoder_4_out4, AOR
  Multiplexer #(.disabled(0), .enable("true")) multiplexer_5 (
    .in0(xor_7_p4), .in1(Flag_Cout), .out(Cin), .sel(IOp[3]), .en(or_10_out));
  Comparator #(.width(16), .mode("unsigned")) comparator_8 (
    .a(Ab), .b(16'hfffe), .eq(comparator_8_eq));  // open: gt, lt
  Comparator #(.width(16), .mode("unsigned")) comparator_9 (
    .a(Ab), .b(16'hfffb), .eq(comparator_9_eq));  // open: gt, lt
  Comparator #(.width(16), .mode("unsigned")) comparator_10 (
    .a(Ab), .b(16'hfffa), .eq(comparator_10_eq));  // open: gt, lt
  Comparator #(.width(16), .mode("unsigned")) comparator_11 (
    .a(Ab), .b(16'hfff9), .eq(comparator_11_eq));  // open: gt, lt
  Comparator #(.width(16), .mode("unsigned")) comparator_12 (
    .a(Ab), .b(16'hfff8), .eq(comparator_12_eq));  // open: gt, lt
  and and_15 (CX, Mov, Is_CX);
  Register #(.width(12), .trigger("falling")) PS (
    .D({or_19_out, Boot_0, 1'b1}),
    .Q({Intr, Pop, Mov, Act, Addr, Jsr, Push, Load_2, Load_1, Load_0, Boot_1, PS_q[0]}), .clk(CLK), .clr(RST));  // open: en
  and and_16 (and_16_out, ~IA[0], ~IA[1], IA[2]);  // AND_Gate
  nand nand_2 (nand_2_out, IX[0], IX[1], IX[2]);
  // AND_Gate and_17: pin names not known; wires that end beside it: CX, or_13_out, AADD
  not not_7 (Boot_0, PS_q[0]);
  Demultiplexer #(.disabled(0)) demultiplexer_2 (
    .out0(demultiplexer_2_out0), .out1(demultiplexer_2_out1), .in(multiplexer_6_out), .sel(IY));
  Multiplexer #(.disabled(0), .enable("true")) multiplexer_6 (
    .in0(and_16_out), .in1(Is_ST), .out(multiplexer_6_out), .sel(IY), .en(nand_2_out));
  Register Mode (
    .D(Db[7:0]), .en(comparator_8_eq),
    .Q({Mode_q[7], No_Timer_Wake, No_Button_Wake, Screen_Disable, Mode_q[3], Timer_IRQ, Timer_NMI, Timer_Enable}),
    .clk(CLK), .clr(RST));
  or or_16 (or_16_out, comparator_10_eq, Timer_Read);
  Multiplexer #(.width(16)) multiplexer_7 (.in0(Db), .in1(Timer_q), .out(multiplexer_7_out), .sel(Timer_Read));
  // OR_Gate or_17: pin names not known; wires that end beside it: Boot_1, Pop, or_17_p3
  Demultiplexer #(.disabled(0)) demultiplexer_3 (
    .out0(demultiplexer_3_out0), .out1(or_19_out[10]), .in(or_18_out), .sel(demultiplexer_2_out1));  // open: en
  or or_18 (or_18_out, Act, Mov);
  assign {controlled_buffer_38_out[7], Sleep_Deep, Sleep_Light, Sleep_Idle, controlled_buffer_38_out[3], Timer_Ack, Timer_Read, Timer_Write} = comparator_8_eq ? Db[15:8] : 8'bz;  // Controlled_Buffer controlled_buffer_38
  Pull_Resistor pull_resistor_6 (.node({controlled_buffer_38_out[7], Sleep_Deep, Sleep_Light, Sleep_Idle, controlled_buffer_38_out[3], Timer_Ack, Timer_Read, Timer_Write}));
  Register #(.width(16)) Temp_Low (.D(multiplexer_7_out), .en(or_16_out), .Q(Temp_Low_q), .clk(CLK), .clr(RST));
  Register #(.width(16)) Limit_Low (.D(Db), .en(comparator_12_eq), .Q(Limit_Low_q), .clk(CLK), .clr(RST));
  or or_19 (or_19_out[2], demultiplexer_5_out1, or_17_p3, demultiplexer_3_out0);
  Demultiplexer #(.disabled(0)) demultiplexer_4 (
    .out0(demultiplexer_4_out0), .out1(demultiplexer_4_out1), .in(Load_0), .sel(nand_3_out));
  Demultiplexer #(.disabled(0)) demultiplexer_5 (
    .out0(demultiplexer_5_out0), .out1(demultiplexer_5_out1), .in(Addr), .sel(Is_LEA));  // open: en
  not not_8 (not_8_out, nand_2_out);
  nand nand_3 (nand_3_out, IA[0], IA[1], IA[2]);
  nand nand_4 (nand_4_out, IB[0], IB[1], IB[2]);
  or or_20 (or_20_out, comparator_9_eq, Timer_Read);
  Multiplexer #(.width(16)) multiplexer_8 (.in0(Db), .in1(Timer_q_2), .out(multiplexer_8_out), .sel(Timer_Read));
  or or_21 (or_21_out[2], R6, R4);
  Multiplexer #(.width(3), .disabled(0)) multiplexer_9 (
    .in0(IA), .in1(IB), .out(multiplexer_9_out), .sel(IY));  // open: en
  Demultiplexer #(.disabled(0)) demultiplexer_6 (
    .out0(or_19_out[4]), .out1(demultiplexer_6_out1), .in(or_22_p3), .sel(nand_4_out));
  // OR_Gate or_22: pin names not known; wires that end beside it: demultiplexer_4_out1, Load_1, or_22_p3
  // OR_Gate or_23: pin names not known; wires that end beside it: demultiplexer_6_out1, Load_2, or_23_p3
  Demultiplexer #(.disabled(0)) demultiplexer_7 (
    .out0(or_19_out[5]), .out1(demultiplexer_7_out1), .in(or_23_p3), .sel(nor_2_p2));  // open: en
  // NOR_Gate nor_2: pin names not known; wires that end beside it: demultiplexer_2_out0, nor_2_p2, Is_JSR
  Register #(.width(16)) Temp_High (.D(multiplexer_8_out), .en(or_20_out), .Q(Temp_High_q), .clk(CLK), .clr(RST));
  Register #(.width(16)) Limit_High (.D(Db), .en(comparator_11_eq), .Q(Limit_High_q), .clk(CLK), .clr(RST));
  Multiplexer #(.width(3), .disabled(0)) multiplexer_10 (
    .in0(multiplexer_9_out), .in1(IB), .out(multiplexer_10_out), .sel(Mov));  // open: en
  Demultiplexer #(.disabled(0)) demultiplexer_8 (
    .out0(or_19_out[3]), .out1(or_19_out[11]), .in(demultiplexer_4_out0), .sel(Is_INTR));  // open: en
  Demultiplexer #(.disabled(0)) demultiplexer_9 (
    .out0(or_19_out[6]), .out1(demultiplexer_9_out1), .in(Push), .sel(not_9_out));  // open: en
  or or_24 (or_24_out, Jsr, Jsr, demultiplexer_7_out1);
  Demultiplexer #(.disabled(0)) demultiplexer_10 (
    .out0(demultiplexer_10_out0), .out1(demultiplexer_10_out1), .in(or_24_out), .sel(not_8_out));  // open: en
  not not_9 (not_9_out, Is_JSR);
  // AND_Gate and_18: pin names not known; wires that end beside it: IOp[4], IOp[5], Is_LEA
  and and_19 (and_19_out, IRQ, IRQ_Enable, undriven);
  or or_25 (or_25_out, and_19_out, and_19_out, and_20_out, and_20_out);
  and and_20 (and_20_out, undriven, NMI, NMI_Enable);
  Counter #(.width(32), .max('hffffffff)) Timer (
    .load(Timer_Write), .D({Temp_High_q, Temp_Low_q}), .Q({Timer_q_2, Timer_q}), .clk(TCLK), .clr(RST));  // open: count, carry
  and and_21 (TCLK, CLK, or_26_out);
  or or_26 (or_26_out, Timer_Write, Timer_Enable);
  assign A = or_21_out[2] ? {or_21_out[2], R6, 1'b0} : 3'bz;  // Controlled_Buffer controlled_buffer_39
  assign A = Addr ? IX : 3'bz;  // Controlled_Buffer controlled_buffer_40
  Pull_Resistor pull_resistor_7 (.node(A));
  assign A = Rp ? IA : 3'bz;  // Controlled_Buffer controlled_buffer_41
  assign B = or_21_out[2] ? {or_21_out[2], R6, 1'b0} : 3'bz;  // Controlled_Buffer controlled_buffer_42
  assign B = Addr ? multiplexer_10_out : 3'bz;  // Controlled_Buffer controlled_buffer_43
  Pull_Resistor pull_resistor_8 (.node(B));
  assign B = Rp ? IB : 3'bz;  // Controlled_Buffer controlled_buffer_44
  assign D = or_21_out[2] ? {or_21_out[2], R6, 1'b0} : 3'bz;  // Controlled_Buffer controlled_buffer_45
  Pull_Resistor pull_resistor_9 (.node(D));
  assign D = Addr ? IA : 3'bz;  // Controlled_Buffer controlled_buffer_46
  assign D = Rp ? IA : 3'bz;  // Controlled_Buffer controlled_buffer_47
  or or_27 (or_19_out[7], demultiplexer_9_out1, demultiplexer_10_out0);
  or or_28 (or_28_out, demultiplexer_10_out1, demultiplexer_5_out0);
  Demultiplexer #(.disabled(0)) demultiplexer_11 (
    .out0(or_19_out[8]), .out1(or_19_out[9]), .in(or_28_out), .sel(IOp[5]));  // open: en
  // AND_Gate and_22: pin names not known; wires that end beside it: or_25_out, INT_prog, Is_INTR
  S_R_Flip_Flop s_r_ff_1 (.Q(s_r_ff_1_q), .preset(comparator_13_eq), .reset(Timer_Ack));  // open: S, clk, R, Qn, en
  Comparator #(.width(32), .mode("unsigned")) comparator_13 (
    .a({Timer_q_2, Timer_q}), .b({Limit_High_q, Limit_Low_q}), .eq(comparator_13_eq));  // open: gt, lt
  Pull_Resistor pull_resistor_10 (.node(IRQ));
  Pull_Resistor pull_resistor_11 (.node(NMI));
  and and_23 (NMI, s_r_ff_1_q, Timer_NMI, s_r_ff_1_q);
  and and_24 (IRQ, Timer_NMI, Timer_IRQ);
  Multiplexer multiplexer_11 (.in0(Flag_Cout), .in1(Flag_SCout), .out(multiplexer_11_out), .sel(IOp[1]));  // open: en
  and and_25 (and_25_out, Addr, Is_LEA);
  nor nor_3 (nor_3_out, IOp[5], and_25_out, Mov);
  // AND_Gate and_26: pin names not known; wires that end beside it: multiplexer_11_out, and_26_p2, multiplexer_11_out, Flag_Zero, Flag_Zero, and_26_p6
  // AND_Gate and_27: pin names not known; wires that end beside it: Flag_Zero, and_26_p2, multiplexer_11_out, multiplexer_11_out, and_27_p5
  // OR_Gate or_29: pin names not known; wires that end beside it: Pop, or_29_p2, Push
  // AND_Gate and_28: pin names not known; wires that end beside it: Addr, Is_LEA, and_28_p3
  and and_29 (and_29_out, IX[0], IX[1], IX[2]);
  Multiplexer #(.select(2), .disabled(0)) multiplexer_12 (
    .in0(and_26_p6), .in1(and_27_p5), .in2(Flag_Zero), .in3(multiplexer_11_out), .out(multiplexer_12_out),
    .sel({IOp[2], IOp[0]}));  // open: en
  not not_10 (not_10_out, IOp[3]);
  // AND_Gate and_30: pin names not known; wires that end beside it: IOp[1], and_30_p2, IOp[2]
  Multiplexer multiplexer_13 (
    .in0(multiplexer_12_out), .in1(not_10_out), .out(multiplexer_13_out), .sel(and_30_p2));  // open: en
  and and_31 (Is_JSR, ~IOp[0], IOp[1], IOp[2], IOp[3], IOp[5]);  // AND_Gate
  and and_32 (Is_CX, IOp[0], IOp[1], IOp[2], IOp[3], IOp[5]);
  or or_30 (or_30_out, Boot_0, Boot_1, Load_0);
  // OR_Gate or_31: pin names not known; wires that end beside it: Load_1, Load_1, Load_2, INC
  buf and_33 (and_33_out, ~Addr);  // AND_Gate AND_Gate
  Demultiplexer #(.disabled(0), .enable("true")) demultiplexer_12 (
    .out0(demultiplexer_12_out0), .out1(demultiplexer_12_out1), .in(Addr), .sel(IY), .en(not_11_out));
  not not_11 (not_11_out, and_28_p3);
  // AND_Gate and_34: pin names not known; wires that end beside it: CMP, Act, and_34_p3
  ExactlyOne xor_8 (.out(xor_8_out), .in1(multiplexer_13_out), .in3(IOp[3]), .in4(IOp[3]));
  or or_32 (Cond_met, xor_8_out, nor_3_out);
  or or_33 (R6, INC, or_30_out, Jsr);
  // OR_Gate or_34: pin names not known; wires that end beside it: Load_1, demultiplexer_12_out0, Si0
  // OR_Gate or_35: pin names not known; wires that end beside it: Push, Pop, R4
  or or_36 (RM, INC, Boot_1, and_33_out);
  or or_37 (or_37_out, or_30_out, Mov, and_28_p3, or_29_p2, and_34_p3);
  // OR_Gate or_38: pin names not known; wires that end beside it: Load_2, demultiplexer_12_out1, Si1
  // OR_Gate or_39: pin names not known; wires that end beside it: Addr, Push, SAr
  or or_40 (Rp, Mov, Act);
  and and_35 (WR, or_37_out, Cond_met);

  // Other names for the same wires on the sheet: PF (some bits) = {Flag_SCout, Flag_Cout, Flag_Zero, INT_prog, IRQ_Enable, NMI_Enable};
  //   Ra = Addr

  // Notes on the sheet:
  //   PbA
  //   PbB
  //   Rb
  //   Db
  //   Ab
  //   buffer_1 drives only 1 and floats otherwise
  //   buffer_2 drives only 1 and floats otherwise
  //   Registers file
  //   Memory
  //   contents of rom_1 (hex, n*v repeats v):
  //   0 0 4 d9a6 7f26 feff ee36 4 41e6 0 ce66 0 d266 53e6 fff6 7191 7111 7110 d9a6 48 65 6c 6c 6f 2c 20 57
  //   6f 72 6c 64 21
  //   User interface
  //   Arithmetic and Logic Unit
  //   SHL
  //   SHR
  //   Flags register
  //   Crappy UART maybe of
  //   MMIO length
  //   ALU decoder
  //   Instruction unpacker
  //   ADD
  //   SUB
  //   CMP
  //   AND
  //   OR
  //   XOR
  //   SHL
  //   SHR
  //   CC
  //   MATH1
  //   PASS
  //   Timer 0
  //   State machine
  //   Register decoder
  //   and_23 drives only 1 and floats otherwise
  //   and_24 drives only 1 and floats otherwise
  //   Condition decoder
  //   Miscellaneous decoders
  //   LT
  //   GT
  //   EQ
  //   CS
endmodule

module _32x16_screen_controller (
  input  CLOCK,
  input  RESET,
  input  Enable,
  input  [15:0] Data,
  input  [15:0] Adress,
  output [15:0] Col_0,
  output [15:0] Col_1,
  output [15:0] Col_2,
  output [15:0] Col_3,
  output [15:0] Col_4,
  output [15:0] Col_5,
  output [15:0] Col_6,
  output [15:0] Col_7,
  output [15:0] Col_8,
  output [15:0] Col_9,
  output [15:0] Col_10,
  output [15:0] Col_11,
  output [15:0] Col_12,
  output [15:0] Col_13,
  output [15:0] Col_14,
  output [15:0] Col_15,
  output [15:0] Col_16,
  output [15:0] Col_17,
  output [15:0] Col_18,
  output [15:0] Col_19,
  output [15:0] Col_20,
  output [15:0] Col_21,
  output [15:0] Col_22,
  output [15:0] Col_23,
  output [15:0] Col_24,
  output [15:0] Col_25,
  output [15:0] Col_26,
  output [15:0] Col_27,
  output [15:0] Col_28,
  output [15:0] Col_29,
  output [15:0] Col_30,
  output [15:0] Col_31
);

  wire and_1_out, and_2_out, comparator_1_lt, decoder_1_out0, decoder_1_out1, decoder_1_out2, decoder_1_out3,
       decoder_1_out4, decoder_1_out5, decoder_1_out6, decoder_1_out7, decoder_1_out8, decoder_1_out9,
       decoder_1_out10, decoder_1_out11, decoder_1_out12, decoder_1_out13, decoder_1_out14, decoder_1_out15,
       decoder_1_out16, decoder_1_out17, decoder_1_out18, decoder_1_out19, decoder_1_out20, decoder_1_out21,
       decoder_1_out22, decoder_1_out23, decoder_1_out24, decoder_1_out25, decoder_1_out26, decoder_1_out27,
       decoder_1_out28, decoder_1_out29, decoder_1_out30, decoder_1_out31, subtractor_1_bout;
  wire [4:0] bit_extender_1_out;
  wire [15:0] subtractor_1_out;

  Subtractor #(.width(16)) subtractor_1 (
    .a(Adress), .b(16'hffc0), .out(subtractor_1_out), .bout(subtractor_1_bout));  // open: bin
  buf and_1 (and_1_out, Enable);  // AND_Gate AND_Gate
  Bit_Extender #(.in_width(16), .out_width(5)) bit_extender_1 (.in(subtractor_1_out), .out(bit_extender_1_out));
  Comparator #(.width(16), .mode("unsigned")) comparator_1 (
    .a(subtractor_1_out), .b(16'h20), .lt(comparator_1_lt));  // open: gt, eq
  Decoder #(.select(5), .disabled(0), .enable("true")) decoder_1 (
    .out0(decoder_1_out0), .out1(decoder_1_out1), .out2(decoder_1_out2), .out3(decoder_1_out3),
    .out4(decoder_1_out4), .out5(decoder_1_out5), .out6(decoder_1_out6), .out7(decoder_1_out7),
    .out8(decoder_1_out8), .out9(decoder_1_out9), .out10(decoder_1_out10), .out11(decoder_1_out11),
    .out12(decoder_1_out12), .out13(decoder_1_out13), .out14(decoder_1_out14), .out15(decoder_1_out15),
    .out16(decoder_1_out16), .out17(decoder_1_out17), .out18(decoder_1_out18), .out19(decoder_1_out19),
    .out20(decoder_1_out20), .out21(decoder_1_out21), .out22(decoder_1_out22), .out23(decoder_1_out23),
    .out24(decoder_1_out24), .out25(decoder_1_out25), .out26(decoder_1_out26), .out27(decoder_1_out27),
    .out28(decoder_1_out28), .out29(decoder_1_out29), .out30(decoder_1_out30), .out31(decoder_1_out31),
    .sel(bit_extender_1_out), .en(and_2_out));
  and and_2 (and_2_out, comparator_1_lt, and_1_out);
  Register #(.width(16)) register_1 (
    .D({Data[0], Data[1], Data[2], Data[3], Data[4], Data[5], Data[6], Data[7], Data[8], Data[9], Data[10], Data[11], Data[12], Data[13], Data[14], Data[15]}),
    .en(decoder_1_out0), .Q(Col_0), .clk(CLOCK), .clr(RESET));
  Register #(.width(16)) register_2 (
    .D({Data[0], Data[1], Data[2], Data[3], Data[4], Data[5], Data[6], Data[7], Data[8], Data[9], Data[10], Data[11], Data[12], Data[13], Data[14], Data[15]}),
    .en(decoder_1_out1), .Q(Col_1), .clk(CLOCK), .clr(RESET));
  Register #(.width(16)) register_3 (
    .D({Data[0], Data[1], Data[2], Data[3], Data[4], Data[5], Data[6], Data[7], Data[8], Data[9], Data[10], Data[11], Data[12], Data[13], Data[14], Data[15]}),
    .en(decoder_1_out2), .Q(Col_2), .clk(CLOCK), .clr(RESET));
  Register #(.width(16)) register_4 (
    .D({Data[0], Data[1], Data[2], Data[3], Data[4], Data[5], Data[6], Data[7], Data[8], Data[9], Data[10], Data[11], Data[12], Data[13], Data[14], Data[15]}),
    .en(decoder_1_out3), .Q(Col_3), .clk(CLOCK), .clr(RESET));
  Register #(.width(16)) register_5 (
    .D({Data[0], Data[1], Data[2], Data[3], Data[4], Data[5], Data[6], Data[7], Data[8], Data[9], Data[10], Data[11], Data[12], Data[13], Data[14], Data[15]}),
    .en(decoder_1_out4), .Q(Col_4), .clk(CLOCK), .clr(RESET));
  Register #(.width(16)) register_6 (
    .D({Data[0], Data[1], Data[2], Data[3], Data[4], Data[5], Data[6], Data[7], Data[8], Data[9], Data[10], Data[11], Data[12], Data[13], Data[14], Data[15]}),
    .en(decoder_1_out5), .Q(Col_5), .clk(CLOCK), .clr(RESET));
  Register #(.width(16)) register_7 (
    .D({Data[0], Data[1], Data[2], Data[3], Data[4], Data[5], Data[6], Data[7], Data[8], Data[9], Data[10], Data[11], Data[12], Data[13], Data[14], Data[15]}),
    .en(decoder_1_out6), .Q(Col_6), .clk(CLOCK), .clr(RESET));
  Register #(.width(16)) register_8 (
    .D({Data[0], Data[1], Data[2], Data[3], Data[4], Data[5], Data[6], Data[7], Data[8], Data[9], Data[10], Data[11], Data[12], Data[13], Data[14], Data[15]}),
    .en(decoder_1_out7), .Q(Col_7), .clk(CLOCK), .clr(RESET));
  Register #(.width(16)) register_9 (
    .D({Data[0], Data[1], Data[2], Data[3], Data[4], Data[5], Data[6], Data[7], Data[8], Data[9], Data[10], Data[11], Data[12], Data[13], Data[14], Data[15]}),
    .en(decoder_1_out8), .Q(Col_8), .clk(CLOCK), .clr(RESET));
  Register #(.width(16)) register_10 (
    .D({Data[0], Data[1], Data[2], Data[3], Data[4], Data[5], Data[6], Data[7], Data[8], Data[9], Data[10], Data[11], Data[12], Data[13], Data[14], Data[15]}),
    .en(decoder_1_out9), .Q(Col_9), .clk(CLOCK), .clr(RESET));
  Register #(.width(16)) register_11 (
    .D({Data[0], Data[1], Data[2], Data[3], Data[4], Data[5], Data[6], Data[7], Data[8], Data[9], Data[10], Data[11], Data[12], Data[13], Data[14], Data[15]}),
    .en(decoder_1_out10), .Q(Col_10), .clk(CLOCK), .clr(RESET));
  Register #(.width(16)) register_12 (
    .D({Data[0], Data[1], Data[2], Data[3], Data[4], Data[5], Data[6], Data[7], Data[8], Data[9], Data[10], Data[11], Data[12], Data[13], Data[14], Data[15]}),
    .en(decoder_1_out11), .Q(Col_11), .clk(CLOCK), .clr(RESET));
  Register #(.width(16)) register_13 (
    .D({Data[0], Data[1], Data[2], Data[3], Data[4], Data[5], Data[6], Data[7], Data[8], Data[9], Data[10], Data[11], Data[12], Data[13], Data[14], Data[15]}),
    .en(decoder_1_out12), .Q(Col_12), .clk(CLOCK), .clr(RESET));
  Register #(.width(16)) register_14 (
    .D({Data[0], Data[1], Data[2], Data[3], Data[4], Data[5], Data[6], Data[7], Data[8], Data[9], Data[10], Data[11], Data[12], Data[13], Data[14], Data[15]}),
    .en(decoder_1_out13), .Q(Col_13), .clk(CLOCK), .clr(RESET));
  Register #(.width(16)) register_15 (
    .D({Data[0], Data[1], Data[2], Data[3], Data[4], Data[5], Data[6], Data[7], Data[8], Data[9], Data[10], Data[11], Data[12], Data[13], Data[14], Data[15]}),
    .en(decoder_1_out14), .Q(Col_14), .clk(CLOCK), .clr(RESET));
  Register #(.width(16)) register_16 (
    .D({Data[0], Data[1], Data[2], Data[3], Data[4], Data[5], Data[6], Data[7], Data[8], Data[9], Data[10], Data[11], Data[12], Data[13], Data[14], Data[15]}),
    .en(decoder_1_out15), .Q(Col_15), .clk(CLOCK), .clr(RESET));
  Register #(.width(16)) register_17 (
    .D({Data[0], Data[1], Data[2], Data[3], Data[4], Data[5], Data[6], Data[7], Data[8], Data[9], Data[10], Data[11], Data[12], Data[13], Data[14], Data[15]}),
    .en(decoder_1_out16), .Q(Col_16), .clk(CLOCK), .clr(RESET));
  Register #(.width(16)) register_18 (
    .D({Data[0], Data[1], Data[2], Data[3], Data[4], Data[5], Data[6], Data[7], Data[8], Data[9], Data[10], Data[11], Data[12], Data[13], Data[14], Data[15]}),
    .en(decoder_1_out17), .Q(Col_17), .clk(CLOCK), .clr(RESET));
  Register #(.width(16)) register_19 (
    .D({Data[0], Data[1], Data[2], Data[3], Data[4], Data[5], Data[6], Data[7], Data[8], Data[9], Data[10], Data[11], Data[12], Data[13], Data[14], Data[15]}),
    .en(decoder_1_out18), .Q(Col_18), .clk(CLOCK), .clr(RESET));
  Register #(.width(16)) register_20 (
    .D({Data[0], Data[1], Data[2], Data[3], Data[4], Data[5], Data[6], Data[7], Data[8], Data[9], Data[10], Data[11], Data[12], Data[13], Data[14], Data[15]}),
    .en(decoder_1_out19), .Q(Col_19), .clk(CLOCK), .clr(RESET));
  Register #(.width(16)) register_21 (
    .D({Data[0], Data[1], Data[2], Data[3], Data[4], Data[5], Data[6], Data[7], Data[8], Data[9], Data[10], Data[11], Data[12], Data[13], Data[14], Data[15]}),
    .en(decoder_1_out20), .Q(Col_20), .clk(CLOCK), .clr(RESET));
  Register #(.width(16)) register_22 (
    .D({Data[0], Data[1], Data[2], Data[3], Data[4], Data[5], Data[6], Data[7], Data[8], Data[9], Data[10], Data[11], Data[12], Data[13], Data[14], Data[15]}),
    .en(decoder_1_out21), .Q(Col_21), .clk(CLOCK), .clr(RESET));
  Register #(.width(16)) register_23 (
    .D({Data[0], Data[1], Data[2], Data[3], Data[4], Data[5], Data[6], Data[7], Data[8], Data[9], Data[10], Data[11], Data[12], Data[13], Data[14], Data[15]}),
    .en(decoder_1_out22), .Q(Col_22), .clk(CLOCK), .clr(RESET));
  Register #(.width(16)) register_24 (
    .D({Data[0], Data[1], Data[2], Data[3], Data[4], Data[5], Data[6], Data[7], Data[8], Data[9], Data[10], Data[11], Data[12], Data[13], Data[14], Data[15]}),
    .en(decoder_1_out23), .Q(Col_23), .clk(CLOCK), .clr(RESET));
  Register #(.width(16)) register_25 (
    .D({Data[0], Data[1], Data[2], Data[3], Data[4], Data[5], Data[6], Data[7], Data[8], Data[9], Data[10], Data[11], Data[12], Data[13], Data[14], Data[15]}),
    .en(decoder_1_out24), .Q(Col_24), .clk(CLOCK), .clr(RESET));
  Register #(.width(16)) register_26 (
    .D({Data[0], Data[1], Data[2], Data[3], Data[4], Data[5], Data[6], Data[7], Data[8], Data[9], Data[10], Data[11], Data[12], Data[13], Data[14], Data[15]}),
    .en(decoder_1_out25), .Q(Col_25), .clk(CLOCK), .clr(RESET));
  Register #(.width(16)) register_27 (
    .D({Data[0], Data[1], Data[2], Data[3], Data[4], Data[5], Data[6], Data[7], Data[8], Data[9], Data[10], Data[11], Data[12], Data[13], Data[14], Data[15]}),
    .en(decoder_1_out26), .Q(Col_26), .clk(CLOCK), .clr(RESET));
  Register #(.width(16)) register_28 (
    .D({Data[0], Data[1], Data[2], Data[3], Data[4], Data[5], Data[6], Data[7], Data[8], Data[9], Data[10], Data[11], Data[12], Data[13], Data[14], Data[15]}),
    .en(decoder_1_out27), .Q(Col_27), .clk(CLOCK), .clr(RESET));
  Register #(.width(16)) register_29 (
    .D({Data[0], Data[1], Data[2], Data[3], Data[4], Data[5], Data[6], Data[7], Data[8], Data[9], Data[10], Data[11], Data[12], Data[13], Data[14], Data[15]}),
    .en(decoder_1_out28), .Q(Col_28), .clk(CLOCK), .clr(RESET));
  Register #(.width(16)) register_30 (
    .D({Data[0], Data[1], Data[2], Data[3], Data[4], Data[5], Data[6], Data[7], Data[8], Data[9], Data[10], Data[11], Data[12], Data[13], Data[14], Data[15]}),
    .en(decoder_1_out29), .Q(Col_29), .clk(CLOCK), .clr(RESET));
  Register #(.width(16)) register_31 (
    .D({Data[0], Data[1], Data[2], Data[3], Data[4], Data[5], Data[6], Data[7], Data[8], Data[9], Data[10], Data[11], Data[12], Data[13], Data[14], Data[15]}),
    .en(decoder_1_out30), .Q(Col_30), .clk(CLOCK), .clr(RESET));
  Register #(.width(16)) register_32 (
    .D({Data[0], Data[1], Data[2], Data[3], Data[4], Data[5], Data[6], Data[7], Data[8], Data[9], Data[10], Data[11], Data[12], Data[13], Data[14], Data[15]}),
    .en(decoder_1_out31), .Q(Col_31), .clk(CLOCK), .clr(RESET));

  // Notes on the sheet:
  //   Adress: pull=down
  //   Enable: pull=up
  //   Data: pull=down
  //   RESET: pull=down
  //   CLOCK: pull=down
  //   Mapped address
endmodule

module Button_inputs (
  input  Left,
  input  Up,
  input  Down,
  input  Right,
  input  Start,
  input  Select,
  input  X,
  input  A,
  input  Y,
  input  B,
  input  Clock,
  input  Clear_interrupt,
  input  Reset,
  output [15:0] Data_out,
  output Interrupt
);

  wire and_1_out, comparator_1_eq, or_1_out;
  wire [15:0] register_1_q;

  Pull_Resistor pull_resistor_1 (.node({Data_out[15:10], Select, Start, B, A, Y, X, Right, Down, Up, Left}));
  and and_1 (and_1_out, Clock, Clear_interrupt, Reset);
  or or_1 (or_1_out, and_1_out, Reset);
  Comparator #(.width(16)) comparator_1 (
    .a({Data_out[15:10], Select, Start, B, A, Y, X, Right, Down, Up, Left}), .b(register_1_q),
    .eq(comparator_1_eq));  // open: gt, lt
  Register #(.width(16)) register_1 (
    .D({Data_out[15:10], Select, Start, B, A, Y, X, Right, Down, Up, Left}), .Q(register_1_q), .clk(or_1_out));  // open: en, clr
  not not_1 (Interrupt, comparator_1_eq);

  assign Data_out[9:0] = {Select, Start, B, A, Y, X, Right, Down, Up, Left};
endmodule
